# Fritzing sketch robot (saved by Fritzing 0.9.2b)
circuit board: 8.46667cm x 5.64444cm
breadboards: 1

parts:
  R7 = PHOTOCELL [package=photocell]
  R8 = PHOTOCELL [package=photocell]
  R5 = Resistor [tolerance=±5% resistance=10k package=THT]
  R1 = Resistor [tolerance=±5% resistance=10k package=THT]
  R2 = Resistor [tolerance=±5% resistance=10k package=THT]
  R3 = Resistor [tolerance=±5% resistance=10k package=THT]
  R4 = Resistor [tolerance=±5% resistance=10k package=THT]
  R6 = Resistor [tolerance=±5% resistance=10k package=THT]
  Launchpad1 = TI Launchpad MSP430G2
  BAT1 = BC9VPC [package=bc9vpc]
  U1 = Voltage Regulator - 3.3V [package="TO220 [THT]"]

nets:
  N1: R7.P$1, R2.Pin_0
  N2: R7.P$2, R8.P$1, R1.Pin_0, R6.Pin_0, Launchpad1.p1, U1.GND
  N3: R8.P$2, R5.Pin_0
  N4: R5.Pin_1, R2.Pin_1, R3.Pin_1, R4.Pin_1, Launchpad1.p20
  N5: R1.Pin_1, R3.Pin_0
  N6: R4.Pin_0, R6.Pin_1
  N7: BAT1.V+, U1.input_voltage
  N8: BAT1.V-, U1.output_voltage
